# Fritzing sketch Controller_diagram (saved by Fritzing 0.9.3b)
breadboards: 1

parts:
  R1 = Rotary Potentiometer (Small) [maximum_resistance=100kΩ package=THT]
  C1 = Electrolytic Capacitor [capacitance=100µF voltage=16V package="100 mil [THT, electrolytic]"]
  R2 = Resistor [tolerance=±5% resistance=10k package=THT]
  R3 = Resistor [tolerance=±5% resistance=10k package=THT]
  S1 = Pushbutton [package="[THT]"]
  R4 = Resistor [tolerance=±5% resistance=10k package=THT]
  R5 = Resistor [tolerance=±5% resistance=1k package=THT]
  R6 = Resistor [tolerance=±5% resistance=1k package=THT]
  R7 = Resistor [tolerance=±5% resistance=1k package=THT]
  LED1 = LED - 5mm [color="Red (633nm)" package="5 mm [THT]"]
  LED2 = LED - 5mm [color="Green (555nm)" package="5 mm [THT]"]
  LED3 = LED - 5mm [color="Blue (470nm)" package="5 mm [THT]"]
  Part1 = Arduino Uno (Rev3)

nets (from the schematic view):
  N1: R1.leg1, R7.Pin_1, LED2.anode, LED3.cathode, LED3.anode, Part1.GND
  N2: R1.wiper, Part1.A1
  N3: R1.leg2, C1.+, R2.Pin_0, R3.Pin_0, S1.Pin_3, S1.Pin_4, Part1.5V
  N4: C1.-, R4.Pin_0, R5.Pin_1, R6.Pin_1, LED1.anode, LED2.cathode
  N5: R2.Pin_1, Part1.A5/SCL
  N6: R3.Pin_1, Part1.A4/SDA
  N7: S1.Pin_1, S1.Pin_2, R4.Pin_1, Part1.D4
  N8: R5.Pin_0, Part1.D5_PWM
  N9: R6.Pin_0, Part1.D6_PWM
  N10: R7.Pin_0, Part1.D7
