# Fritzing sketch Lights_diagram (saved by Fritzing 0.9.3b)
breadboards: 1

parts:
  Componente1 = Arduino Uno (Rev3)
  R1 = Resistor [tolerance=±5% resistance=220 package=THT]
  S1 = Pushbutton [package="[THT]"]
  LED1 = LED - 5mm [color="Red (633nm)" package="5 mm [THT]"]
  R2 = Resistor [tolerance=±5% resistance=220 package=THT]
  R3 = Resistor [tolerance=±5% resistance=220 package=THT]
  LED2 = LED - 5mm [color="Green (555nm)" package="5 mm [THT]"]
  LED3 = LED - 5mm [color="Red (633nm)" package="5 mm [THT]"]
  R4 = Resistor [tolerance=±5% resistance=220 package=THT]
  LED4 = LED - 5mm [color="Yellow (595nm)" package="5 mm [THT]"]
  R5 = Resistor [tolerance=±5% resistance=220 package=THT]
  LED5 = LED - 5mm [color="Green (555nm)" package="5 mm [THT]"]
  R6 = Resistor [tolerance=±5% resistance=220 package=THT]
  R7 = Resistor [tolerance=±5% resistance=10k package=THT]
  R8 = Resistor [tolerance=±5% resistance=10k package=THT]

nets (from the schematic view):
  N1: Componente1.A4/SDA, R8.Pin_0
  N2: Componente1.A5/SCL, R7.Pin_0
  N3: Componente1.D8, LED3.anode
  N4: Componente1.D10_PWM/SS, R2.Pin_0
  N5: Componente1.D11_PWM/MOSI, R3.Pin_0
  N6: Componente1.D13/SCK, R1.Pin_0, S1.Pin_1, S1.Pin_2
  N7: Componente1.D2, LED5.anode
  N8: Componente1.D3_PWM, LED5.cathode, R6.Pin_0
  N9: Componente1.D5_PWM, LED4.anode
  N10: Componente1.D6_PWM, LED4.cathode, R5.Pin_0
  N11: Componente1.D7, LED3.cathode, R4.Pin_0
  N12: Componente1.5V, S1.Pin_3, S1.Pin_4, R7.Pin_1, R8.Pin_1
  N13: Componente1.GND, R1.Pin_1, LED1.cathode, LED2.cathode, R4.Pin_1, R5.Pin_1, R6.Pin_1
  N14: LED1.anode, R2.Pin_1
  N15: R3.Pin_1, LED2.anode
